// Digital circuit main.dig as structural Verilog
module main (
  input  clk,
  input  reset,
  output [23:0] pc_out,
  output [31:0] mem_din,
  output [31:0] ir_bus,
  output [21:0] ir_offset,
  output [21:0] ir_addr,
  output [5:0] ir_addr_w,
  output [5:0] ir_addr_b,
  output [2:0] wb_sel,
  output [9:0] ir_opcode,
  output [7:0] ctrl_alu_op,
  output [31:0] alu_out,
  output [31:0] reg_w_data,
  output [31:0] p,
  output [15:0] term_data,
  output [15:0] vram_addr,
  output term_we,
  output [23:0] pc_save,
  output [31:0] m_out,
  output [23:0] mem_addr,
  output [2:0] ctrl_w_sel,
  output [31:0] reg_b,
  output [31:0] reg_a,
  output ctrl_reg_we,
  output [5:0] ir_addr_a,
  output [3:0] ir_sel
);

  wire alu_cout, alu_nout, alu_nzout, alu_vout, alu_zout, and_1_out, bank_en, comparator_1_eq,
       comparator_2_eq, cond, ctrl_branch_en, ctrl_bus_sel, ctrl_cin_sel, ctrl_cycles, ctrl_flags_we,
       ctrl_jump_type, ctrl_mem_rd, ctrl_mem_sel, ctrl_mem_wr, ctrl_pc_src, ctrl_shift_op, flag_c, flag_n,
       flag_v, flag_z, HALT_IN, is_mmio, mem_rd_out, ram_cs, seq_exec, seq_fetch, vram_we;
  wire [1:0] c_addr_msb2;
  wire [3:0] BANK_SEL;
  wire [4:0] ctrl_alu_pre;
  wire [15:0] vram_data;
  wire [23:0] CPU_ADDR_OUT, mmio_addr;
  wire [31:0] io_data_in, mul_out, reg_c, shift_out;

  // program_counter program_counter_1: pin names not known; wires that end beside it: mem_din, alu_out, ctrl_pc_src, ir_offset, reset, ctrl_cycles, clk, flag_n, flag_c, flag_z, flag_v, cond, ctrl_jump_type, ctrl_branch_en, pc_out, pc_save, seq_fetch, seq_exec
  register register_1 (
    .WE(ctrl_reg_we), .DATA_W(reg_w_data), .ADDR_A(ir_addr_a), .ADDR_B(ir_addr_b), .ADDR_W(ir_addr_w),
    .EXEC(seq_exec), .clk(clk), .BANK_SEL(BANK_SEL), .Bank_en(bank_en), .DATA_A(reg_a), .DATA_B(reg_b),
    .DATA_C(reg_c));
  // ir ir_1: pin names not known; wires that end beside it: mem_din, seq_fetch, clk, ir_sel, reg_b, ir_opcode, ir_addr_a, ir_addr_b, ir_addr_w, ir_addr, ir_offset, cond, ir_bus, BANK_SEL
  // bus_arbitration bus_arbitration_1: pin names not known; wires that end beside it: seq_fetch, ir_addr, ctrl_mem_rd, ctrl_bus_sel, reg_b, pc_out, {24{1'b0}}, alu_out, mem_addr, mem_rd_out
  io_controller io_controller_1 (
    .mem_addr(mmio_addr), .c_wr(ctrl_mem_wr), .kb_data(16'h1), .mem_data_out(reg_b), .io_data_in(io_data_in),
    .ram_cs(ram_cs), .vram_we(vram_we), .vram_addr(vram_addr), .vram_data(vram_data), .term_we(term_we),
    .term_data(term_data));
  RAMDualPort #(.AddrBits(24), .Bits(32)) ramdualport_1 (
    .A(CPU_ADDR_OUT), .Din(reg_b), .str(ctrl_mem_wr), .C(clk), .ld(mem_rd_out), .D(m_out));
  // microcode microcode_1: pin names not known; wires that end beside it: ir_opcode, ctrl_alu_op, ctrl_alu_pre, ctrl_cin_sel, ctrl_shift_op, ir_sel, bank_en, ctrl_w_sel, ctrl_reg_we, ctrl_flags_we, ctrl_mem_rd, ctrl_mem_wr, ctrl_mem_sel, ctrl_branch_en, ctrl_jump_type, ctrl_cycles, ctrl_bus_sel, ctrl_pc_src
  mmio_bus mmio_bus_1 (
    .ADDR(mem_addr), .CPU_ADDR_OUT(CPU_ADDR_OUT), .mmio_addr(mmio_addr), .is_mmio(is_mmio),
    .cpu_addr_msb2(c_addr_msb2));
  Comparator #(.Bits(6)) comparator_1 (.a(6'b000010), .b(ir_addr_w), .eq(comparator_1_eq));  // open: gt, lt
  mul_div mul_div_1 (.A(reg_a), .B(ir_bus), .mul_out(mul_out));
  // byte_lane_decoder byte_lane_decoder_1: pin names not known; wires that end beside it: m_out, ctrl_mem_sel, io_data_in, c_addr_msb2, mem_din
  and and_1 (and_1_out, seq_exec, ctrl_reg_we, comparator_1_eq);
  // shift shift_1: pin names not known; wires that end beside it: reg_a, ctrl_shift_op, ir_bus, shift_out
  alu_32b_final alu_32b_final_1 (
    .A(reg_a), .nz0(1'b0), .B(ir_bus), .Opcode(ctrl_alu_op), .control(ctrl_alu_pre), .REG_C(reg_c),
    .cin_sel(ctrl_cin_sel), .FLAG_C(flag_c), .vout(alu_vout), .zout(alu_zout), .nzout(alu_nzout),
    .nout(alu_nout), .Out(alu_out), .cout(alu_cout));
  // flag_reg flag_reg_1: pin names not known; wires that end beside it: alu_zout, alu_cout, alu_nout, alu_vout, ctrl_flags_we, clk, seq_exec, mem_din, flag_z, flag_c, flag_n, flag_v
  wb_mux wb_mux_1 (
    .wb_sel(ctrl_w_sel), .alu_out(alu_out), .shift_out(shift_out), .pc_save(pc_save), .mem_din(io_data_in),
    .io_datain(reg_a), .reg_a(ir_bus), .ir_bus(mul_out), .reg_w_data(reg_w_data));
  Register #(.Bits(32)) register_2 (.D(reg_w_data), .C(clk), .en(and_1_out), .Q(p));
  and and_2 (HALT_IN, comparator_2_eq, seq_exec);
  Comparator #(.Bits(10)) comparator_2 (.a(10'hff), .b(ir_opcode), .eq(comparator_2_eq));  // open: gt, lt

  assign wb_sel = ctrl_w_sel;

  // Other names for the same wires on the sheet: ctrl_wb_sel[2:0] = ctrl_w_sel; mem_ram_out[31:0] = m_out
endmodule

/* Test case add-arithmetic-only:
reset clk alu-out ir-opcode ctrl-alu-op
1 0 x x x
1 1 x x x
1 0 x x x
# EXECUTE ADDI R0=0: microcode dispatches alu-op=0x96 (XOR3/ADD)
1 1 0 0x10 0x96
1 0 x x x
1 1 x x x
1 0 x x x
# EXECUTE ADDI R1=10: R0+imm=0+10=10
1 1 10 0x10 0x96
1 0 x x x
1 1 x x x
1 0 x x x
# EXECUTE ADDI R2=10: R0+imm=0+10=10
1 1 10 0x10 0x96
1 0 x x x
1 1 x x x
1 0 x x x
# EXECUTE ADD R2+=R1: post-writeback alu-out=R2_new+R1=20+10=30
1 1 30 0x01 0x96
1 0 x x x
1 1 x x x
1 0 x x x
# EXECUTE JMP: ALU unused, ctrl-alu-op=0x00
1 1 x 0x62 0x00
*/

/* Test case load-store-chain:
reset clk alu-out ctrl-reg-we ir-opcode
# Counter loop (picks up mid-run, R2 already at 40 after lw-pipeline test above)
# This is an independent run — 3 more ADD iterations: 20, 30, 40
1 0 x x x
1 1 x x x
1 0 x x x
1 1 x x x
1 0 x x x
1 1 x x x
1 0 x x x
1 1 x x x
1 0 x x x
1 1 x x x
1 0 x x x
1 1 x x x
1 0 x x x
# ADD first iteration: R2=20
1 1 20 1 0x01
1 0 x x x
1 1 x x x
1 0 x x x
1 1 x 0 0x62
1 0 x x x
1 1 x x x
1 0 x x x
# ADD second iteration: R2=30
1 1 30 1 0x01
*/

/* Test case lw-pipeline:
reset clk alu-out ctrl-reg-we ir-opcode pc-out
# EEPROM: ADDI R0=0 -> ADDI R1=10 -> ADDI R2=10 -> ADD R2+=R1 -> JMP 3 (loop)
# Counter: R2 increments by 10 each iteration (10+10=20, 20+10=30, ...)
1 0 x x x x
1 1 x x x x
1 0 x x x x
# EXECUTE ADDI R0=r0+0=0
1 1 0 1 0x10 1
1 0 x x x x
1 1 x x x x
1 0 x x x x
# EXECUTE ADDI R1=r0+10=10
1 1 10 1 0x10 2
1 0 x x x x
1 1 x x x x
1 0 x x x x
# EXECUTE ADDI R2=r0+10=10
1 1 10 1 0x10 3
1 0 x x x x
1 1 x x x x
1 0 x x x x
# EXECUTE ADD iter1: R2 written=20, write-through re-reads R2=20, shows 20+10=30
1 1 30 1 0x01 4
1 0 x x x x
1 1 x x x x
1 0 x x x x
# EXECUTE JMP 3 — PC reloads to word 3
1 1 x 0 0x62 3
1 0 x x x x
1 1 x x x x
1 0 x x x x
# EXECUTE ADD iter2: R2 written=30, shows 30+10=40
1 1 40 1 0x01 4
1 0 x x x x
1 1 x x x x
1 0 x x x x
# EXECUTE JMP — PC back to 3
1 1 x 0 0x62 3
1 0 x x x x
1 1 x x x x
1 0 x x x x
# EXECUTE ADD iter3: R2 written=40, shows 40+10=50
1 1 50 1 0x01 4
*/

/* Test case program counter:
reset clk pc-out ir-opcode
# EEPROM loop: ADDI x3, ADD, JMP rel 3 (0x62000003, IR[0]=1)
1 0 x x
1 1 x x
1 0 x x
1 1 1 0x10
1 0 x x
1 1 x x
1 0 x x
1 1 2 0x10
1 0 x x
1 1 x x
1 0 x x
1 1 3 0x10
1 0 x x
1 1 x x
1 0 x x
1 1 4 0x01
1 0 x x
1 1 x x
1 0 x x
1 1 3 0x62
*/
